# Fritzing sketch 2-Axis Gimbal (saved by Fritzing 0.9.3b)
breadboards: 1

parts:
  Teensy_3_1 = Teensy 3.1
  Part2 = Triple Axis Accelerometer Breakout - ADXL345
  R1 = Resistor [tolerance=±5% resistance=4.7k package=THT]
  R2 = Resistor [tolerance=±5% resistance=4.7k package=THT]
  Servo_1 = Basic Servo
  Servo_2 = Basic Servo

nets:
  GND: Teensy_3_1.GND, Part2.GND, Part2.SDO, Servo_1.gnd, Servo_2.gnd
  N1: Teensy_3_1.3V3#15, Part2.VCC, Part2.CS, R1.Pin_0, R2.Pin_0
  N2: Teensy_3_1.A4/D18, Part2.SDA, R1.Pin_1
  N3: Teensy_3_1.A5/D19, Part2.SCL, R2.Pin_1
  N4: Teensy_3_1.A6/D20, Servo_1.pulse
  N5: Teensy_3_1.A7/D21, Servo_2.pulse
  VCC: Teensy_3_1.Vin, Servo_1.vcc, Servo_2.vcc
